# Fritzing sketch Schema1 (saved by Fritzing 0.8.7b)
breadboards: 1

parts:
  QB = NPN-Transistor [package="TO92 [THT]"]
  RA = Resistor [tolerance=±5% resistance=1.6k package=THT]
  RB = Resistor [tolerance=±5% resistance=1.6k package=THT]
  QC = PNP-Transistor [package="TO92 [THT]"]
  RC = Resistor [tolerance=±5% resistance=1.6k package=THT]
  QA = NPN-Transistor [package="TO92 [THT]"]
  RY = Resistor [tolerance=±5% resistance=1.6k package=THT]
  VCC1 = 4 x AAA Battery Mount

nets:
  N1: QB.E, QC.C, RY.Pin_0
  N2: QB.B, RB.Pin_1
  5V: QB.C, RA.Pin_1, QC.E, QA.E, QA.B, QA.C
  N3: QC.B, RC.Pin_0
  GND: RY.Pin_1, VCC1.-

notes:
  A
  B
  Y
  C
