# Fritzing sketch Schema2 (saved by Fritzing 0.8.7b)
breadboards: 1

parts:
  RY = Resistor [tolerance=±5% resistance=1.6k package=THT]
  QA = NPN-Transistor [package="TO92 [THT]"]
  RA = Resistor [tolerance=±5% resistance=1.6k package=THT]
  QB = PNP-Transistor [package="TO92 [THT]"]
  RB = Resistor [tolerance=±5% resistance=1.6k package=THT]
  QC = NPN-Transistor [package="TO92 [THT]"]
  RC = Resistor [tolerance=±5% resistance=1.6k package=THT]
  VCC1 = 4 x AAA Battery Mount

nets:
  N1: RY.Pin_0, VCC1.+
  N2: RY.Pin_1, QA.C
  N3: QA.E, QB.E, QC.C
  N4: QA.B, RA.Pin_1
  N5: QB.B, RB.Pin_1
  N6: QB.C, QC.E, VCC1.-
  N7: QC.B, RC.Pin_0

notes:
  A
  B
  Y
  C
