# Fritzing sketch Schema1 (saved by Fritzing 0.8.7b)
breadboards: 1

parts:
  VCC1 = 4 x AAA Battery Mount
  R1 = Resistor [tolerance=±5% resistance=1.6k package=THT]
  LED1 = LEDs [package=led10mm]

nets:
  GND: VCC1.-, R1.Pin_1
  N1: VCC1.+, LED1.A
  N2: R1.Pin_0, LED1.C
