# Fritzing sketch Schema2 (saved by Fritzing 0.8.7b)
breadboards: 1

parts:
  LED2 = LEDs [package=led10mm]
  U1_A = IC, DIP package, 14 pins [chip_label=SN7407]
  R2 = Resistor [tolerance=±5% resistance=1.6k package=THT]
  VCC1 = 4 x AAA Battery Mount

nets:
  N1: LED2.A, R2.Pin_1
  N2: LED2.C, U1_A.pin2
  GND: U1_A.pin1
  N3: U1_A.pin7, VCC1.-
  N4: U1_A.pin14, VCC1.+
