# Fritzing sketch Schema4 (saved by Fritzing 0.8.7b)
breadboards: 1

parts:
  R2 = Resistor [tolerance=±5% resistance=1.6k package=THT]
  R2_2 = Resistor [tolerance=±5% resistance=1.6k package=THT]
  LED2 = LEDs [package=led10mm]
  U1_C = IC, DIP package, 14 pins [chip_label=SN7407]
  VCC1 = 4 x AAA Battery Mount
  S1 = SWITCH-MOMENTARY-2 [package=tactile_switch_smd-2]

nets:
  5V: R2.Pin_0, R2_2.Pin_0
  N1: R2.Pin_1, U1_C.pin5, S1.1
  N2: R2_2.Pin_1, LED2.A, U1_C.pin6
  GND: LED2.C, S1.2
  N3: U1_C.pin7, VCC1.-
  N4: U1_C.pin14, VCC1.+
