# Fritzing sketch 2SketchShiftRight (saved by Fritzing 0.8.7b)
breadboards: 1

parts:
  IC2 = IC, DIP package, 14 pins [chip_label=SN7495]
  JP9 = Header 4 [package=molex-1x4_lock]  # not connected
  S3 = Pushbutton [package="[THT]"]  # not connected
  S4 = Pushbutton [package="[THT]"]  # not connected
  JP10 = Header 4 [package=molex-1x4_lock]
  JP11 = Header 4 [package=molex-1x4_lock]
  JP12 = Header 6 [package=molex-1x6_lock]
  JP13 = Header 3 [package=screwterminal-3.5mm-3_lock.007s]  # not connected
  JP14 = Header 3 [package=screwterminal-3.5mm-3_lock.007s]
  JP15 = Header 3 [package=screwterminal-3.5mm-3_lock.007s]
  JP16 = Header 3 [package=screwterminal-3.5mm-3_lock.007s]  # not connected
  VCC2 = 4 x AAA Battery Mount
  R9 = Resistor [tolerance=±5% resistance=4.6k package=THT]
  R10 = Resistor [tolerance=±5% resistance=4.6k package=THT]
  R11 = Resistor [tolerance=±5% resistance=4.6k package=THT]
  R12 = Resistor [tolerance=±5% resistance=4.6k package=THT]
  R14 = Resistor [tolerance=±5% resistance=4.6k package=THT]
  R16 = Resistor [tolerance=±5% resistance=4.6k package=THT]
  R17 = Resistor [tolerance=±5% resistance=4.6k package=THT]
  R18 = Resistor [tolerance=±5% resistance=4.6k package=THT]
  R19 = Resistor [tolerance=±5% resistance=4.6k package=THT]
  R20 = Resistor [tolerance=±5% resistance=4.6k package=THT]

nets:
  N1: IC2.pin1, IC2.pin2, IC2.pin7, JP15.3
  N2: IC2.pin8, R14.Pin_0, R14.Pin_1
  N3: IC2.pin9, IC2.pin14, JP14.3, R11.Pin_0, R11.Pin_1
  N4: IC2.pin10, JP11.1, R16.Pin_0, R16.Pin_1
  N5: IC2.pin11, JP11.2, R12.Pin_0, R12.Pin_1
  N6: IC2.pin12, JP11.3, R10.Pin_0, R10.Pin_1
  N7: IC2.pin13, JP11.4, R9.Pin_0, R9.Pin_1
  N8: JP10.1, R17.Pin_0
  N9: JP10.2, R18.Pin_0
  N10: JP10.3, R19.Pin_0
  N11: JP10.4, R20.Pin_0
  N12: JP12.1, R17.Pin_1
  N13: JP12.2, R18.Pin_1
  N14: JP12.3, R19.Pin_1
  N15: JP12.4, R20.Pin_1
  N16: JP14.1, VCC2.+
  N17: JP15.1, VCC2.-

notes:
  DOWN
  UP
  J1
  J2
  J3
  Trigger Down
  Trigger UP
  LED2
  LED6
  LED5
  LED4
  LED3
  LED1
  GND
  5V
  J4
