# Fritzing sketch 3SketchShiftLeft (saved by Fritzing 0.8.7b)
breadboards: 1

parts:
  JP17 = Header 4 [package=molex-1x4_lock]  # not connected
  IC3 = IC, DIP package, 14 pins [chip_label=SN7495]
  S5 = Pushbutton [package="[THT]"]  # not connected
  S6 = Pushbutton [package="[THT]"]  # not connected
  JP18 = Header 4 [package=molex-1x4_lock]
  JP19 = Header 4 [package=molex-1x4_lock]
  JP20 = Header 6 [package=molex-1x6_lock]
  JP21 = Header 3 [package=screwterminal-3.5mm-3_lock.007s]  # not connected
  JP22 = Header 3 [package=screwterminal-3.5mm-3_lock.007s]
  JP23 = Header 3 [package=screwterminal-3.5mm-3_lock.007s]
  JP24 = Header 3 [package=screwterminal-3.5mm-3_lock.007s]  # not connected
  VCC3 = 4 x AAA Battery Mount
  R21 = Resistor [tolerance=±5% resistance=4.6k package=THT]
  R22 = Resistor [tolerance=±5% resistance=4.6k package=THT]
  R23 = Resistor [tolerance=±5% resistance=4.6k package=THT]
  R24 = Resistor [tolerance=±5% resistance=4.6k package=THT]
  R25 = Resistor [tolerance=±5% resistance=4.6k package=THT]
  R26 = Resistor [tolerance=±5% resistance=4.6k package=THT]
  R27 = Resistor [tolerance=±5% resistance=4.6k package=THT]
  R28 = Resistor [tolerance=±5% resistance=4.6k package=THT]
  R29 = Resistor [tolerance=±5% resistance=4.6k package=THT]
  R30 = Resistor [tolerance=±5% resistance=4.6k package=THT]
  R31 = Resistor [tolerance=±5% resistance=4.6k package=THT]
  R32 = Resistor [tolerance=±5% resistance=4.6k package=THT]

nets:
  N1: IC3.pin1, R31.Pin_1
  N2: IC3.pin6, R32.Pin_1
  N3: IC3.pin7, JP23.3
  N4: IC3.pin8, IC3.pin14, JP22.3, R29.Pin_0, R29.Pin_1, R31.Pin_0, R32.Pin_0
  N5: IC3.pin9, R27.Pin_0, R27.Pin_1
  N6: IC3.pin10, JP19.1, R30.Pin_0, R30.Pin_1
  N7: IC3.pin11, JP19.2, R28.Pin_0, R28.Pin_1
  N8: IC3.pin12, JP19.3, R26.Pin_0, R26.Pin_1
  N9: IC3.pin13, JP19.4, R23.Pin_0, R23.Pin_1
  N10: JP18.1, R24.Pin_0
  N11: JP18.2, R22.Pin_0
  N12: JP18.3, R21.Pin_0
  N13: JP18.4, R25.Pin_0
  N14: JP20.1, R24.Pin_1
  N15: JP20.2, R22.Pin_1
  N16: JP20.3, R21.Pin_1
  N17: JP20.4, R25.Pin_1
  N18: JP22.1, VCC3.+
  N19: JP23.1, VCC3.-

notes:
  DOWN
  UP
  J1
  J2
  J3
  Trigger Down
  Trigger UP
  LED2
  LED6
  LED5
  LED4
  LED3
  LED1
  GND
  5V
  J4
