# Fritzing sketch SN7474AsincronCLR (saved by Fritzing 0.8.7b)
breadboards: 1

parts:
  S13 = Pushbutton [package="[THT]"]  # not connected
  JP49 = Header 4 [package=molex-1x4_lock]  # not connected
  S14 = Pushbutton [package="[THT]"]  # not connected
  JP50 = Header 4 [package=molex-1x4_lock]
  JP51 = Header 4 [package=molex-1x4_lock]
  JP52 = Header 6 [package=molex-1x6_lock]
  JP53 = Header 3 [package=screwterminal-3.5mm-3_lock.007s]
  JP54 = Header 3 [package=screwterminal-3.5mm-3_lock.007s]  # not connected
  JP55 = Header 3 [package=screwterminal-3.5mm-3_lock.007s]  # not connected
  JP56 = Header 3 [package=screwterminal-3.5mm-3_lock.007s]
  VCC7 = 4 x AAA Battery Mount
  IC4 = IC, DIP package, 14 pins [chip_label=SN7474]
  R3 = Resistor [tolerance=±5% resistance=4.6k package=THT]
  R4 = Resistor [tolerance=±5% resistance=4.6k package=THT]

nets:
  N1: JP50.1, R4.Pin_0
  N2: JP50.2, R3.Pin_0
  N3: JP51.1, IC4.pin4
  N4: JP51.2, JP56.1, IC4.pin1, IC4.pin7
  N5: JP52.1, R4.Pin_1
  N6: JP52.2, R3.Pin_1
  N7: JP52.5, IC4.pin5
  N8: JP52.6, IC4.pin6
  N9: JP53.1, IC4.pin14
  N10: JP53.3, VCC7.+
  N11: JP56.3, VCC7.-

notes:
  DOWN
  UP
  J1
  J2
  J3
  Trigger Down
  Trigger UP
  LED2
  LED6
  LED5
  LED4
  LED3
  LED1
  GND
  5V
  J4
  Count Bit 1
  Count Bit 3
  Count Bit 2
  Count Bit 0
  J6
  J5
