# Fritzing sketch SN7475 (saved by Fritzing 0.8.7b)
breadboards: 1

parts:
  S7 = Pushbutton [package="[THT]"]  # not connected
  JP25 = Header 4 [package=molex-1x4_lock]  # not connected
  S8 = Pushbutton [package="[THT]"]  # not connected
  JP26 = Header 4 [package=molex-1x4_lock]
  JP27 = Header 4 [package=molex-1x4_lock]
  JP28 = Header 6 [package=molex-1x6_lock]
  JP29 = Header 3 [package=screwterminal-3.5mm-3_lock.007s]
  JP30 = Header 3 [package=screwterminal-3.5mm-3_lock.007s]  # not connected
  JP31 = Header 3 [package=screwterminal-3.5mm-3_lock.007s]  # not connected
  JP32 = Header 3 [package=screwterminal-3.5mm-3_lock.007s]
  VCC4 = 4 x AAA Battery Mount
  IC1 = IC, DIP package, 16 pins [chip_label=SN7475]

nets:
  N1: JP26.1, JP28.1
  N2: JP26.2, JP28.2
  N3: JP27.1, IC1.pin2
  N4: JP27.2, IC1.pin13
  N5: JP28.5, IC1.pin16
  N6: JP28.6, IC1.pin1
  N7: JP29.1, IC1.pin5
  N8: JP29.3, VCC4.+
  N9: JP32.1, IC1.pin12
  N10: JP32.3, VCC4.-

notes:
  DOWN
  UP
  J1
  J2
  J3
  Trigger Down
  Trigger UP
  LED2
  LED6
  LED5
  LED4
  LED3
  LED1
  GND
  5V
  J4
  Count Bit 0
  Count Bit 2
  Count Bit 3
  Count Bit 1
  J5
  J6
