# Fritzing sketch SN74S112ANAsincronCLR (saved by Fritzing 0.8.7b)
breadboards: 1

parts:
  JP57 = Header 4 [package=molex-1x4_lock]  # not connected
  S15 = Pushbutton [package="[THT]"]  # not connected
  S16 = Pushbutton [package="[THT]"]  # not connected
  JP58 = Header 4 [package=molex-1x4_lock]
  JP59 = Header 4 [package=molex-1x4_lock]
  JP60 = Header 6 [package=molex-1x6_lock]
  JP61 = Header 3 [package=screwterminal-3.5mm-3_lock.007s]
  JP62 = Header 3 [package=screwterminal-3.5mm-3_lock.007s]  # not connected
  JP63 = Header 3 [package=screwterminal-3.5mm-3_lock.007s]  # not connected
  JP64 = Header 3 [package=screwterminal-3.5mm-3_lock.007s]
  VCC8 = 4 x AAA Battery Mount
  IC5 = IC, DIP package, 16 pins [chip_label=SN74S112AN]
  R3 = Resistor [tolerance=±5% resistance=4.6k package=THT]
  R4 = Resistor [tolerance=±5% resistance=4.6k package=THT]

nets:
  N1: JP58.1, R4.Pin_0
  N2: JP58.2, R3.Pin_0
  N3: JP59.1, IC5.pin4
  N4: JP59.2, JP64.1, IC5.pin8, IC5.pin15
  N5: JP60.1, R4.Pin_1
  N6: JP60.2, R3.Pin_1
  N7: JP60.5, IC5.pin5
  N8: JP60.6, IC5.pin6
  N9: JP61.1, IC5.pin16
  N10: JP61.3, VCC8.+
  N11: JP64.3, VCC8.-

notes:
  DOWN
  UP
  J1
  J2
  J3
  Trigger Down
  Trigger UP
  LED2
  LED6
  LED5
  LED4
  LED3
  LED1
  GND
  5V
  J4
  Count Bit 1
  Count Bit 3
  Count Bit 2
  Count Bit 0
  J6
  J5
