# Fritzing sketch Schema3 (saved by Fritzing 0.8.7b)
breadboards: 1

parts:
  U1_B = IC, DIP package, 14 pins [chip_label=SN7407]
  R2 = Resistor [tolerance=±5% resistance=1.6k package=THT]
  LED2 = LEDs [package=led10mm]
  VCC1 = 4 x AAA Battery Mount

nets:
  GND: U1_B.pin3, LED2.C
  N1: U1_B.pin4, R2.Pin_1, LED2.A
  N2: U1_B.pin7, VCC1.-
  N3: U1_B.pin14, VCC1.+
  5V: R2.Pin_0
