# Fritzing sketch 1Sketch (saved by Fritzing 0.8.7b)
breadboards: 1

parts:
  JP1 = Header 4 [package=molex-1x4_lock]  # not connected
  S1 = Pushbutton [package="[THT]"]  # not connected
  S2 = Pushbutton [package="[THT]"]  # not connected
  JP5 = Header 3 [package=screwterminal-3.5mm-3_lock.007s]  # not connected
  JP6 = Header 3 [package=screwterminal-3.5mm-3_lock.007s]
  JP7 = Header 3 [package=screwterminal-3.5mm-3_lock.007s]  # not connected
  JP8 = Header 3 [package=screwterminal-3.5mm-3_lock.007s]
  VCC1 = 4 x AAA Battery Mount
  JP4 = Header 4 [package=molex-1x4_lock]  # not connected
  JP2 = Header 4 [package=molex-1x4_lock]  # not connected
  JP3 = Header 6 [package=molex-1x6_lock]  # not connected
  R1 = Resistor [tolerance=±5% resistance=4.6k package=THT]
  R2 = Resistor [tolerance=±5% resistance=4.6k package=THT]
  R3 = Resistor [tolerance=±5% resistance=4.6k package=THT]
  R4 = Resistor [tolerance=±5% resistance=4.6k package=THT]
  R5 = Resistor [tolerance=±5% resistance=4.6k package=THT]
  R6 = Resistor [tolerance=±5% resistance=4.6k package=THT]
  R7 = Resistor [tolerance=±5% resistance=4.6k package=THT]
  IC1 = IC, DIP package, 14 pins [chip_label=SN7495]
  R8 = Resistor [tolerance=±5% resistance=4.6k package=THT]

nets:
  N1: JP6.1, VCC1.-
  N2: JP6.3, IC1.pin3, IC1.pin4, IC1.pin6, IC1.pin7
  N3: JP8.1, VCC1.+
  N4: JP8.3, R1.Pin_0, R6.Pin_0, R7.Pin_0, R7.Pin_1, IC1.pin8, IC1.pin14
  N5: R1.Pin_1, IC1.pin1
  N6: R2.Pin_0, R2.Pin_1, IC1.pin10
  N7: R3.Pin_0, R3.Pin_1, IC1.pin11
  N8: R4.Pin_0, R4.Pin_1, IC1.pin12
  N9: R5.Pin_0, R5.Pin_1, IC1.pin13
  N10: R6.Pin_1, IC1.pin5
  N11: IC1.pin9, R8.Pin_0, R8.Pin_1

notes:
  DOWN
  UP
  J1
  J2
  J3
  Trigger Down
  Trigger UP
  LED1
  LED2
  LED3
  LED4
  LED5
  LED6
  GND
  5V
  J4
