# Fritzing sketch SN7474Sincron (saved by Fritzing 0.8.7b)
breadboards: 1

parts:
  S9 = Pushbutton [package="[THT]"]  # not connected
  JP33 = Header 4 [package=molex-1x4_lock]  # not connected
  S10 = Pushbutton [package="[THT]"]  # not connected
  JP34 = Header 4 [package=molex-1x4_lock]
  JP35 = Header 4 [package=molex-1x4_lock]
  JP36 = Header 6 [package=molex-1x6_lock]
  JP37 = Header 3 [package=screwterminal-3.5mm-3_lock.007s]
  JP38 = Header 3 [package=screwterminal-3.5mm-3_lock.007s]  # not connected
  JP39 = Header 3 [package=screwterminal-3.5mm-3_lock.007s]  # not connected
  JP40 = Header 3 [package=screwterminal-3.5mm-3_lock.007s]
  VCC5 = 4 x AAA Battery Mount
  IC2 = IC, DIP package, 14 pins [chip_label=SN7474]

nets:
  N1: JP34.1, JP36.1
  N2: JP34.2, JP36.2
  N3: JP35.1, IC2.pin3
  N4: JP35.2, IC2.pin2
  N5: JP36.5, IC2.pin5
  N6: JP36.6, IC2.pin6
  N7: JP37.1, IC2.pin14
  N8: JP37.3, VCC5.+
  N9: JP40.1, IC2.pin7
  N10: JP40.3, VCC5.-

notes:
  DOWN
  UP
  J1
  J2
  J3
  Trigger Down
  Trigger UP
  LED2
  LED6
  LED5
  LED4
  LED3
  LED1
  GND
  5V
  J4
  Count Bit 1
  Count Bit 3
  Count Bit 2
  Count Bit 0
  J6
  J5
