# Fritzing sketch SN74S112ANSincron (saved by Fritzing 0.8.7b)
breadboards: 1

parts:
  S11 = Pushbutton [package="[THT]"]  # not connected
  JP41 = Header 4 [package=molex-1x4_lock]  # not connected
  S12 = Pushbutton [package="[THT]"]  # not connected
  JP42 = Header 4 [package=molex-1x4_lock]
  JP43 = Header 4 [package=molex-1x4_lock]
  JP44 = Header 6 [package=molex-1x6_lock]
  JP45 = Header 3 [package=screwterminal-3.5mm-3_lock.007s]
  JP46 = Header 3 [package=screwterminal-3.5mm-3_lock.007s]  # not connected
  JP47 = Header 3 [package=screwterminal-3.5mm-3_lock.007s]  # not connected
  JP48 = Header 3 [package=screwterminal-3.5mm-3_lock.007s]
  VCC6 = 4 x AAA Battery Mount
  IC3 = IC, DIP package, 16 pins [chip_label=SN74S112AN]

nets:
  N1: JP42.1, JP44.1
  N2: JP42.2, JP44.2
  N3: JP42.3, JP44.3
  N4: JP43.1, IC3.pin1
  N5: JP43.2, IC3.pin3
  N6: JP43.3, IC3.pin2
  N7: JP44.5, IC3.pin5
  N8: JP44.6, IC3.pin6
  N9: JP45.1, IC3.pin16
  N10: JP45.3, VCC6.+
  N11: JP48.1, IC3.pin8
  N12: JP48.3, VCC6.-

notes:
  DOWN
  UP
  J1
  J2
  J3
  Trigger Down
  Trigger UP
  LED2
  LED6
  LED5
  LED4
  LED3
  LED1
  GND
  5V
  J4
  Count Bit 1
  Count Bit 3
  Count Bit 2
  Count Bit 0
  J6
  J5
