# Fritzing sketch (A+B)C'SN7400 (saved by Fritzing 0.8.7b)
breadboards: 1

parts:
  JP73 = Header 4 [package=molex-1x4_lock]  # not connected
  S19 = Pushbutton [package="[THT]"]  # not connected
  S20 = Pushbutton [package="[THT]"]  # not connected
  JP74 = Header 4 [package=molex-1x4_lock]
  JP75 = Header 4 [package=molex-1x4_lock]
  JP76 = Header 6 [package=molex-1x6_lock]
  JP77 = Header 3 [package=screwterminal-3.5mm-3_lock.007s]
  JP78 = Header 3 [package=screwterminal-3.5mm-3_lock.007s]  # not connected
  JP79 = Header 3 [package=screwterminal-3.5mm-3_lock.007s]  # not connected
  JP80 = Header 3 [package=screwterminal-3.5mm-3_lock.007s]
  VCC10 = 4 x AAA Battery Mount
  IC2 = IC, DIP package, 14 pins [chip_label=SN7400]
  R5 = Resistor [tolerance=±5% resistance=4k package=THT]
  R6 = Resistor [tolerance=±5% resistance=1k package=THT]
  R7 = Resistor [tolerance=±5% resistance=1k package=THT]
  R8 = Resistor [tolerance=±5% resistance=1k package=THT]
  IC3 = IC, DIP package, 14 pins [chip_label=SN7400]
  R9 = Resistor [tolerance=±5% resistance=1k package=THT]
  R11 = Resistor [tolerance=±5% resistance=1k package=THT]

nets:
  N1: JP74.1, R5.Pin_1
  N2: JP75.1, IC3.pin8
  N3: JP76.1, R5.Pin_0
  N4: JP77.1, R6.Pin_1, R7.Pin_1, R8.Pin_0, R9.Pin_0, R11.Pin_1
  N5: JP77.3, VCC10.+
  N6: JP80.1, IC2.pin7, IC3.pin7
  N7: JP80.3, VCC10.-
  N8: IC2.pin1, IC2.pin2, R7.Pin_0
  N9: IC2.pin3, IC2.pin10
  N10: IC2.pin4, IC2.pin5, R6.Pin_0
  N11: IC2.pin6, IC2.pin9
  N12: IC2.pin8, IC3.pin4
  N13: IC2.pin14, R8.Pin_1
  N14: IC3.pin1, IC3.pin2, R11.Pin_0
  N15: IC3.pin3, IC3.pin5
  N16: IC3.pin6, IC3.pin9, IC3.pin10
  N17: IC3.pin14, R9.Pin_1

notes:
  DOWN
  UP
  J1
  J2
  J3
  Trigger Down
  Trigger UP
  LED2
  LED6
  LED5
  LED4
  LED3
  LED1
  GND
  5V
  J4
  Count Bit 1
  Count Bit 3
  Count Bit 2
  Count Bit 0
  J6
  J5
