# Fritzing sketch FunctiiCircuiteMUX (saved by Fritzing 0.8.7b)
breadboards: 1

parts:
  JP73 = Header 4 [package=molex-1x4_lock]  # not connected
  S19 = Pushbutton [package="[THT]"]  # not connected
  S20 = Pushbutton [package="[THT]"]  # not connected
  JP74 = Header 4 [package=molex-1x4_lock]
  JP75 = Header 4 [package=molex-1x4_lock]
  JP76 = Header 6 [package=molex-1x6_lock]
  JP77 = Header 3 [package=screwterminal-3.5mm-3_lock.007s]
  JP78 = Header 3 [package=screwterminal-3.5mm-3_lock.007s]  # not connected
  JP79 = Header 3 [package=screwterminal-3.5mm-3_lock.007s]  # not connected
  JP80 = Header 3 [package=screwterminal-3.5mm-3_lock.007s]
  VCC10 = 4 x AAA Battery Mount
  R5 = Resistor [tolerance=±5% resistance=4k package=THT]
  IC1 = IC, DIP package, 16 pins [chip_label=CD40257]
  IC2 = IC, DIP package, 16 pins [chip_label=SN74153]
  IC3 = IC, DIP package, 16 pins [chip_label=SN74153]
  R6 = Resistor [tolerance=±5% resistance=1k package=THT]
  R7 = Resistor [tolerance=±5% resistance=1k package=THT]
  R8 = Resistor [tolerance=±5% resistance=1k package=THT]
  R9 = Resistor [tolerance=±5% resistance=1k package=THT]
  R10 = Resistor [tolerance=±5% resistance=1k package=THT]
  R11 = Resistor [tolerance=±5% resistance=1k package=THT]
  R12 = Resistor [tolerance=±5% resistance=1k package=THT]
  R13 = Resistor [tolerance=±5% resistance=1k package=THT]
  R14 = Resistor [tolerance=±5% resistance=1k package=THT]
  R15 = Resistor [tolerance=±5% resistance=1k package=THT]
  R16 = Resistor [tolerance=±5% resistance=1k package=THT]

nets:
  N1: JP74.1, R5.Pin_1
  N2: JP75.1, IC1.pin4
  N3: JP76.1, R5.Pin_0
  N4: JP77.1, JP80.1, IC1.pin8, IC2.pin1, IC2.pin2, IC2.pin8, IC2.pin15, IC3.pin1, IC3.pin2, IC3.pin6, IC3.pin8, IC3.pin14, IC3.pin15, R6.Pin_1, R7.Pin_1, R8.Pin_1, R9.Pin_0, R10.Pin_0, R11.Pin_0, R12.Pin_0, R13.Pin_0, R14.Pin_0, R15.Pin_0, R16.Pin_1
  N5: JP77.3, VCC10.+
  N6: JP80.3, VCC10.-
  N7: IC1.pin1, R16.Pin_0
  N8: IC1.pin2, IC2.pin7
  N9: IC1.pin3, IC3.pin7
  N10: IC1.pin16, R7.Pin_0
  N11: IC2.pin3, R9.Pin_1
  N12: IC2.pin4, R10.Pin_1
  N13: IC2.pin5, R11.Pin_1
  N14: IC2.pin6, R12.Pin_1
  N15: IC2.pin16, R6.Pin_0
  N16: IC3.pin3, R13.Pin_1
  N17: IC3.pin4, R15.Pin_1
  N18: IC3.pin5, R14.Pin_1
  N19: IC3.pin16, R8.Pin_0

notes:
  DOWN
  UP
  J1
  J2
  J3
  Trigger Down
  Trigger UP
  LED2
  LED6
  LED5
  LED4
  LED3
  LED1
  GND
  5V
  J4
  Count Bit 1
  Count Bit 3
  Count Bit 2
  Count Bit 0
  J6
  J5
