# Fritzing sketch XORSN7400 (saved by Fritzing 0.8.7b)
breadboards: 1

parts:
  JP65 = Header 4 [package=molex-1x4_lock]  # not connected
  S17 = Pushbutton [package="[THT]"]  # not connected
  S18 = Pushbutton [package="[THT]"]  # not connected
  JP66 = Header 4 [package=molex-1x4_lock]
  JP67 = Header 4 [package=molex-1x4_lock]
  JP68 = Header 6 [package=molex-1x6_lock]
  JP69 = Header 3 [package=screwterminal-3.5mm-3_lock.007s]
  JP70 = Header 3 [package=screwterminal-3.5mm-3_lock.007s]  # not connected
  JP71 = Header 3 [package=screwterminal-3.5mm-3_lock.007s]  # not connected
  JP72 = Header 3 [package=screwterminal-3.5mm-3_lock.007s]
  VCC9 = 4 x AAA Battery Mount
  IC1 = IC, DIP package, 14 pins [chip_label=SN7400]
  R1 = Resistor [tolerance=±5% resistance=1k package=THT]
  R2 = Resistor [tolerance=±5% resistance=1k package=THT]
  R3 = Resistor [tolerance=±5% resistance=1k package=THT]
  R4 = Resistor [tolerance=±5% resistance=4k package=THT]

nets:
  N1: JP66.1, R4.Pin_1
  N2: JP67.1, IC1.pin11
  N3: JP68.1, R4.Pin_0
  N4: JP69.1, R1.Pin_0, R2.Pin_1, R3.Pin_1
  N5: JP69.3, VCC9.+
  N6: JP72.1, IC1.pin7
  N7: JP72.3, VCC9.-
  N8: IC1.pin1, IC1.pin4, IC1.pin9, R2.Pin_0
  N9: IC1.pin2, R3.Pin_0
  N10: IC1.pin3, IC1.pin5, IC1.pin10
  N11: IC1.pin6, IC1.pin13
  N12: IC1.pin8, IC1.pin12
  N13: IC1.pin14, R1.Pin_1

notes:
  DOWN
  UP
  J1
  J2
  J3
  Trigger Down
  Trigger UP
  LED2
  LED6
  LED5
  LED4
  LED3
  LED1
  GND
  5V
  J4
  Count Bit 1
  Count Bit 3
  Count Bit 2
  Count Bit 0
  J6
  J5
