# Fritzing sketch Numarator13_8 (saved by Fritzing 0.8.7b)
breadboards: 1

parts:
  JP81 = Header 4 [package=molex-1x4_lock]  # not connected
  S21 = Pushbutton [package="[THT]"]  # not connected
  S22 = Pushbutton [package="[THT]"]  # not connected
  JP82 = Header 4 [package=molex-1x4_lock]
  JP83 = Header 4 [package=molex-1x4_lock]
  JP84 = Header 6 [package=molex-1x6_lock]
  JP85 = Header 3 [package=screwterminal-3.5mm-3_lock.007s]
  JP86 = Header 3 [package=screwterminal-3.5mm-3_lock.007s]  # not connected
  JP87 = Header 3 [package=screwterminal-3.5mm-3_lock.007s]  # not connected
  JP88 = Header 3 [package=screwterminal-3.5mm-3_lock.007s]
  VCC11 = 4 x AAA Battery Mount
  R12 = Resistor [tolerance=±5% resistance=4k package=THT]
  IC1 = IC, DIP package, 14 pins [chip_label=74ALS138]
  IC2 = IC, DIP package, 14 pins [chip_label=SN74193]
  R13 = Resistor [tolerance=±5% resistance=4k package=THT]
  R14 = Resistor [tolerance=±5% resistance=4k package=THT]
  R15 = Resistor [tolerance=±5% resistance=4k package=THT]
  R16 = Resistor [tolerance=±5% resistance=4k package=THT]
  R17 = Resistor [tolerance=±5% resistance=4k package=THT]
  R20 = Resistor [tolerance=±5% resistance=4k package=THT]
  R21 = Resistor [tolerance=±5% resistance=4k package=THT]
  R23 = Resistor [tolerance=±5% resistance=4k package=THT]

nets:
  N1: JP82.1, R12.Pin_1
  N2: JP82.2, R13.Pin_1
  N3: JP82.3, R14.Pin_1
  N4: JP82.4, R15.Pin_1
  N5: JP83.1, IC1.pin3, IC2.pin12
  N6: JP83.2, IC1.pin2, IC2.pin11
  N7: JP83.3, IC1.pin1, IC2.pin10
  N8: JP83.4, IC2.pin9
  N9: JP84.1, R12.Pin_0
  N10: JP84.2, R13.Pin_0
  N11: JP84.3, R14.Pin_0
  N12: JP84.4, R15.Pin_0
  N13: JP85.1, R16.Pin_1, R17.Pin_1, R20.Pin_1, R21.Pin_1, R23.Pin_1
  N14: JP85.3, VCC11.+
  N15: JP88.1, IC1.pin4, IC1.pin5, IC2.pin4
  N16: JP88.3, VCC11.-
  N17: IC1.pin6, R17.Pin_0
  N18: IC1.pin13, IC2.pin8
  N19: IC2.pin1, R16.Pin_0
  N20: IC2.pin3, R23.Pin_0
  N21: IC2.pin5, R21.Pin_0
  N22: IC2.pin6, R20.Pin_0

notes:
  DOWN
  UP
  J1
  J2
  J3
  Trigger Down
  Trigger UP
  LED2
  LED6
  LED5
  LED4
  LED3
  LED1
  GND
  5V
  J4
  Count Bit 1
  Count Bit 3
  Count Bit 2
  Count Bit 0
  J6
  J5
