# Fritzing sketch NumaratorDiag_temp (saved by Fritzing 0.8.7b)
breadboards: 1

parts:
  JP89 = Header 4 [package=molex-1x4_lock]  # not connected
  S23 = Pushbutton [package="[THT]"]  # not connected
  S24 = Pushbutton [package="[THT]"]  # not connected
  JP90 = Header 4 [package=molex-1x4_lock]
  JP91 = Header 4 [package=molex-1x4_lock]
  JP92 = Header 6 [package=molex-1x6_lock]
  JP93 = Header 3 [package=screwterminal-3.5mm-3_lock.007s]
  JP94 = Header 3 [package=screwterminal-3.5mm-3_lock.007s]  # not connected
  JP95 = Header 3 [package=screwterminal-3.5mm-3_lock.007s]  # not connected
  JP96 = Header 3 [package=screwterminal-3.5mm-3_lock.007s]
  VCC12 = 4 x AAA Battery Mount
  R24 = Resistor [tolerance=±5% resistance=4k package=THT]
  R25 = Resistor [tolerance=±5% resistance=4k package=THT]
  R26 = Resistor [tolerance=±5% resistance=4k package=THT]
  R27 = Resistor [tolerance=±5% resistance=4k package=THT]
  R28 = Resistor [tolerance=±5% resistance=4k package=THT]
  R29 = Resistor [tolerance=±5% resistance=4k package=THT]
  R30 = Resistor [tolerance=±5% resistance=4k package=THT]
  R31 = Resistor [tolerance=±5% resistance=4k package=THT]
  R32 = Resistor [tolerance=±5% resistance=4k package=THT]
  R33 = Resistor [tolerance=±5% resistance=4k package=THT]
  IC3 = IC, DIP package, 14 pins [chip_label=74ALS138]
  IC4 = IC, DIP package, 14 pins [chip_label=SN74193]

nets:
  N1: JP90.1, R29.Pin_1
  N2: JP90.2, R30.Pin_1
  N3: JP90.3, R31.Pin_1
  N4: JP90.4, R32.Pin_1
  N5: JP91.1, IC3.pin3, IC4.pin12
  N6: JP91.2, IC3.pin2, IC4.pin11
  N7: JP91.3, IC3.pin1, IC4.pin10
  N8: JP91.4, IC4.pin9
  N9: JP92.1, R29.Pin_0
  N10: JP92.2, R30.Pin_0
  N11: JP92.3, R31.Pin_0
  N12: JP92.4, R32.Pin_0
  N13: JP93.1, R24.Pin_1, R25.Pin_1, R26.Pin_1, R27.Pin_1, R28.Pin_1, R33.Pin_1
  N14: JP93.3, VCC12.+
  N15: JP96.1, IC3.pin4, IC3.pin5
  N16: JP96.3, VCC12.-
  N17: R24.Pin_0, IC3.pin6
  N18: R25.Pin_0, IC4.pin6
  N19: R26.Pin_0, IC4.pin3
  N20: R27.Pin_0, IC4.pin4
  N21: R28.Pin_0, IC4.pin5
  N22: R33.Pin_0, IC4.pin1
  N23: IC3.pin14, IC4.pin8

notes:
  DOWN
  UP
  J1
  J2
  J3
  Trigger Down
  Trigger UP
  LED2
  LED6
  LED5
  LED4
  LED3
  LED1
  GND
  5V
  J4
  Count Bit 1
  Count Bit 3
  Count Bit 2
  Count Bit 0
  J6
  J5
